// Logisim project NEGT.circ as structural Verilog: 1 circuit, main circuit NEG
module NEG (
  input  [31:0] XFR1R0N,
  output [23:0] XFA2A1
);

  wire [7:0] not_1_out;

  assign not_1_out = ~XFR1R0N[7:0];  // NOT_Gate not_1, 8 bits wide
  Adder adder_1 (.a(not_1_out), .b(8'h1), .out({XFA2A1[18], XFA2A1[6:0]}), .cin(1'b0));  // open: cout
  and and_1 (XFA2A1[17], ~XFA2A1[0], ~XFA2A1[1], ~XFA2A1[2], ~XFA2A1[3], ~XFA2A1[4], ~XFA2A1[5], ~XFA2A1[6], ~XFA2A1[18]);  // AND_Gate

  assign {XFA2A1[23:19], XFA2A1[16:7]} = {4'b0000, XFR1R0N[27], XFR1R0N[24:16], XFA2A1[18]};
endmodule
