// Logisim project adc.circ as structural Verilog: 1 circuit, main circuit ADC
module ADC (
  input  [31:0] in_1,
  output [23:0] out_2
);

  wire and_2_out, and_3_out;

  and and_1 (out_2[17], ~out_2[0], ~out_2[1], ~out_2[2], ~out_2[3], ~out_2[4], ~out_2[5], ~out_2[6], ~out_2[18]);  // AND_Gate
  and and_2 (and_2_out, ~in_1[7], ~in_1[15], out_2[18]);  // AND_Gate
  and and_3 (and_3_out, in_1[15], in_1[7], ~out_2[18]);  // AND_Gate
  or or_1 (out_2[19], and_2_out, and_3_out);
  sum8 sum8_1 (.n1(in_1[7:0]), .n2(in_1[15:8]), .c(in_1[24]), .res({out_2[18], out_2[6:0]}), .cout(out_2[16]));

  assign {out_2[23:20], out_2[15:7]} = {4'b0000, in_1[23:16], out_2[18]};

  // Other names for the same wires on the sheet: s1 = in_1[7]; s2 = in_1[15]

  // Notes on the sheet:
  //   c
  //   z
  //   s
  //   o
endmodule
