// Logisim project alu.circ as structural Verilog: 1 circuit, main circuit main
module main (
  input  [7:0] N,
  input  [7:0] R0,
  input  [7:0] R1,
  input  [3:0] COSZin,
  input  [4:0] INST,
  output [7:0] ACC,
  output [7:0] ACC2,
  output [3:0] COSZout
);

  wire [3:0] multiplexer_1_out;
  wire [23:0] adc_1_out_2, add_1_out_2, andalu_1_xfa2a1, cbw_1_xfa2a1, dec_1_xfa2a1, idiv_1_xfa2a1,
       imul_1_xfa2a1, inc_1_xfa2a1, neg_1_xfa2a1, notalu_1_xfa2a1, oralu_1_xfa2a1, rcl_1_xfa2a1,
       rcr_1_xfa2a1, rolalu_1_xfa2a1, roralu_1_xfa2a1, sal_1_xfa2a1, sar_1_xfa2a1, sbb_1_xfa2a1,
       shl_1_xfa2a1, shr_1_xfa2a1, sub_1_xfa2a1, xchg_1_xfa2a1, xoralu_1_xfa2a1;

  XCHG xchg_1 (.XFR1R0N({4'b0000, COSZin[2:0], COSZin[3], R1, R0, N}), .XFA2A1(xchg_1_xfa2a1));
  CBW cbw_1 (.XFR1R0N({4'b0000, COSZin[2:0], COSZin[3], R1, R0, N}), .XFA2A1(cbw_1_xfa2a1));
  ADD add_1 (.in_1({4'b0000, COSZin[2:0], COSZin[3], R1, R0, N}), .out_2(add_1_out_2));
  ADC adc_1 (.in_1({4'b0000, COSZin[2:0], COSZin[3], R1, R0, N}), .out_2(adc_1_out_2));
  SUB sub_1 (.XFR1R0N({4'b0000, COSZin[2:0], COSZin[3], R1, R0, N}), .XFA2A1(sub_1_xfa2a1));
  SBB sbb_1 (.XFR1R0N({4'b0000, COSZin[2:0], COSZin[3], R1, R0, N}), .XFA2A1(sbb_1_xfa2a1));
  IDIV idiv_1 (.XFR1R0N({4'b0000, COSZin[2:0], COSZin[3], R1, R0, N}), .XFA2A1(idiv_1_xfa2a1));
  IMUL imul_1 (.XFR1R0N({4'b0000, COSZin[2:0], COSZin[3], R1, R0, N}), .XFA2A1(imul_1_xfa2a1));
  INC inc_1 (.XFR1R0N({4'b0000, COSZin[2:0], COSZin[3], R1, R0, N}), .XFA2A1(inc_1_xfa2a1));
  DEC dec_1 (.XFR1R0N({4'b0000, COSZin[2:0], COSZin[3], R1, R0, N}), .XFA2A1(dec_1_xfa2a1));
  NEG neg_1 (.XFR1R0N({4'b0000, COSZin[2:0], COSZin[3], R1, R0, N}), .XFA2A1(neg_1_xfa2a1));
  SAL sal_1 (.XFR1R0N({4'b0000, COSZin[2:0], COSZin[3], R1, R0, N}), .XFA2A1(sal_1_xfa2a1));
  SAR sar_1 (.XFR1R0N({4'b0000, COSZin[2:0], COSZin[3], R1, R0, N}), .XFA2A1(sar_1_xfa2a1));
  NOTalu notalu_1 (.XFR1R0N({4'b0000, COSZin[2:0], COSZin[3], R1, R0, N}), .XFA2A1(notalu_1_xfa2a1));
  ANDalu andalu_1 (.XFR1R0N({4'b0000, COSZin[2:0], COSZin[3], R1, R0, N}), .XFA2A1(andalu_1_xfa2a1));
  ORalu oralu_1 (.XFR1R0N({4'b0000, COSZin[2:0], COSZin[3], R1, R0, N}), .XFA2A1(oralu_1_xfa2a1));
  XORalu xoralu_1 (.XFR1R0N({4'b0000, COSZin[2:0], COSZin[3], R1, R0, N}), .XFA2A1(xoralu_1_xfa2a1));
  SHL shl_1 (.XFR1R0N({4'b0000, COSZin[2:0], COSZin[3], R1, R0, N}), .XFA2A1(shl_1_xfa2a1));
  SHR shr_1 (.XFR1R0N({4'b0000, COSZin[2:0], COSZin[3], R1, R0, N}), .XFA2A1(shr_1_xfa2a1));
  RCL rcl_1 (.XFR1R0N({4'b0000, COSZin[2:0], COSZin[3], R1, R0, N}), .XFA2A1(rcl_1_xfa2a1));
  RCR rcr_1 (.XFR1R0N({4'b0000, COSZin[2:0], COSZin[3], R1, R0, N}), .XFA2A1(rcr_1_xfa2a1));
  ROLalu rolalu_1 (.XFR1R0N({4'b0000, COSZin[2:0], COSZin[3], R1, R0, N}), .XFA2A1(rolalu_1_xfa2a1));
  RORalu roralu_1 (.XFR1R0N({4'b0000, COSZin[2:0], COSZin[3], R1, R0, N}), .XFA2A1(roralu_1_xfa2a1));
  Multiplexer #(.select(5), .width(24)) multiplexer_1 (
    .in0(xchg_1_xfa2a1), .in1(cbw_1_xfa2a1), .in2(add_1_out_2), .in3(adc_1_out_2), .in4(sub_1_xfa2a1),
    .in5(sbb_1_xfa2a1), .in6(idiv_1_xfa2a1), .in7(imul_1_xfa2a1), .in8(inc_1_xfa2a1), .in9(dec_1_xfa2a1),
    .in10(neg_1_xfa2a1), .in11(sal_1_xfa2a1), .in12(sar_1_xfa2a1), .in13(notalu_1_xfa2a1),
    .in14(andalu_1_xfa2a1), .in15(oralu_1_xfa2a1), .in16(xoralu_1_xfa2a1), .in17(shl_1_xfa2a1),
    .in18(shr_1_xfa2a1), .in19(rcl_1_xfa2a1), .in20(rcr_1_xfa2a1), .in21(rolalu_1_xfa2a1),
    .in22(roralu_1_xfa2a1), .out({multiplexer_1_out, COSZout[2:0], COSZout[3], ACC2, ACC}), .sel(INST));  // open: in23, in24, in25, in26, in27, in28, in29, in30, in31
endmodule
