// Logisim project and.circ as structural Verilog: 1 circuit, main circuit ANDalu
module ANDalu (
  input  [31:0] XFR1R0N,
  output [23:0] XFA2A1
);

  and and_1 (XFA2A1[0], XFR1R0N[0], XFR1R0N[8]);
  and and_2 (XFA2A1[1], XFR1R0N[1], XFR1R0N[9]);
  and and_3 (XFA2A1[2], XFR1R0N[2], XFR1R0N[10]);
  and and_4 (XFA2A1[3], XFR1R0N[3], XFR1R0N[11]);
  and and_5 (XFA2A1[4], XFR1R0N[4], XFR1R0N[12]);
  and and_6 (XFA2A1[5], XFR1R0N[5], XFR1R0N[13]);
  and and_7 (XFA2A1[6], XFR1R0N[6], XFR1R0N[14]);
  and and_8 (XFA2A1[18], XFR1R0N[7], XFR1R0N[15]);
  and and_9 (XFA2A1[17], ~XFA2A1[0], ~XFA2A1[1], ~XFA2A1[2], ~XFA2A1[3], ~XFA2A1[4], ~XFA2A1[5], ~XFA2A1[6], ~XFA2A1[18]);  // AND_Gate

  assign {XFA2A1[23:19], XFA2A1[16:7]} = {4'b0000, XFR1R0N[27], XFR1R0N[24:16], XFA2A1[18]};
endmodule
