// Logisim project cbw.circ as structural Verilog: 1 circuit, main circuit CBW
module CBW (
  input  [31:0] XFR1R0N,
  output [23:0] XFA2A1
);

  Multiplexer #(.width(8)) multiplexer_1 (.in0({8{1'b0}}), .in1({8{1'b1}}), .out(XFA2A1[15:8]), .sel(XFR1R0N[7]));
  and and_1 (XFA2A1[17], ~XFR1R0N[0], ~XFR1R0N[1], ~XFR1R0N[2], ~XFR1R0N[3], ~XFR1R0N[4], ~XFR1R0N[5], ~XFR1R0N[6], ~XFR1R0N[7]);  // AND_Gate

  assign {XFA2A1[23:18], XFA2A1[16], XFA2A1[7:0]} = {4'b0000, XFR1R0N[27], XFR1R0N[7], XFR1R0N[24], XFR1R0N[7:0]};

  // Notes on the sheet:
  //   c
  //   z
  //   s
  //   o
endmodule
