// Logisim project division.circ as structural Verilog: 1 circuit, main circuit div
module div (
  input  [15:0] dividendo,
  input  [7:0] divisor,
  output [7:0] out_3,
  output [7:0] out_4
);

  wire [7:0] divisoriter_1_cocienteout, divisoriter_1_divisorout, divisoriter_1_residuoout,
       divisoriter_2_cocienteout, divisoriter_2_divisorout, divisoriter_2_residuoout,
       divisoriter_3_cocienteout, divisoriter_3_divisorout, divisoriter_3_residuoout,
       divisoriter_4_cocienteout, divisoriter_4_divisorout, divisoriter_4_residuoout,
       divisoriter_5_cocienteout, divisoriter_5_divisorout, divisoriter_5_residuoout,
       divisoriter_6_cocienteout, divisoriter_6_divisorout, divisoriter_6_residuoout,
       divisoriter_7_cocienteout, divisoriter_7_divisorout, divisoriter_7_residuoout,
       divisoriter_8_cocienteout, divisoriter_8_divisorout, divisoriter_8_residuoout,
       divisoriter_9_cocienteout, divisoriter_9_divisorout, divisoriter_9_residuoout,
       divisoriter_10_cocienteout, divisoriter_10_divisorout, divisoriter_10_residuoout,
       divisoriter_11_cocienteout, divisoriter_11_divisorout, divisoriter_11_residuoout,
       divisoriter_12_cocienteout, divisoriter_12_divisorout, divisoriter_12_residuoout,
       divisoriter_13_cocienteout, divisoriter_13_divisorout, divisoriter_13_residuoout,
       divisoriter_14_cocienteout, divisoriter_14_divisorout, divisoriter_14_residuoout,
       divisoriter_15_cocienteout, divisoriter_15_divisorout, divisoriter_15_residuoout;
  wire [15:0] divisoriter_1_dividendoout, divisoriter_2_dividendoout, divisoriter_3_dividendoout,
       divisoriter_4_dividendoout, divisoriter_5_dividendoout, divisoriter_6_dividendoout,
       divisoriter_7_dividendoout, divisoriter_8_dividendoout, divisoriter_9_dividendoout,
       divisoriter_10_dividendoout, divisoriter_11_dividendoout, divisoriter_12_dividendoout,
       divisoriter_13_dividendoout, divisoriter_14_dividendoout, divisoriter_15_dividendoout;

  divisorIter divisoriter_1 (
    .dividendo(dividendo), .divisor(divisor), .cociente({8{1'b0}}), .residuo({8{1'b0}}),
    .dividendoOut(divisoriter_1_dividendoout), .divisorOut(divisoriter_1_divisorout),
    .cocienteOut(divisoriter_1_cocienteout), .residuoOut(divisoriter_1_residuoout));
  divisorIter divisoriter_2 (
    .dividendo(divisoriter_15_dividendoout), .divisor(divisoriter_15_divisorout),
    .cociente(divisoriter_15_cocienteout), .residuo(divisoriter_15_residuoout),
    .dividendoOut(divisoriter_2_dividendoout), .divisorOut(divisoriter_2_divisorout),
    .cocienteOut(divisoriter_2_cocienteout), .residuoOut(divisoriter_2_residuoout));
  divisorIter divisoriter_3 (
    .dividendo(divisoriter_1_dividendoout), .divisor(divisoriter_1_divisorout),
    .cociente(divisoriter_1_cocienteout), .residuo(divisoriter_1_residuoout),
    .dividendoOut(divisoriter_3_dividendoout), .divisorOut(divisoriter_3_divisorout),
    .cocienteOut(divisoriter_3_cocienteout), .residuoOut(divisoriter_3_residuoout));
  divisorIter divisoriter_4 (
    .dividendo(divisoriter_2_dividendoout), .divisor(divisoriter_2_divisorout),
    .cociente(divisoriter_2_cocienteout), .residuo(divisoriter_2_residuoout),
    .dividendoOut(divisoriter_4_dividendoout), .divisorOut(divisoriter_4_divisorout),
    .cocienteOut(divisoriter_4_cocienteout), .residuoOut(divisoriter_4_residuoout));
  divisorIter divisoriter_5 (
    .dividendo(divisoriter_3_dividendoout), .divisor(divisoriter_3_divisorout),
    .cociente(divisoriter_3_cocienteout), .residuo(divisoriter_3_residuoout),
    .dividendoOut(divisoriter_5_dividendoout), .divisorOut(divisoriter_5_divisorout),
    .cocienteOut(divisoriter_5_cocienteout), .residuoOut(divisoriter_5_residuoout));
  divisorIter divisoriter_6 (
    .dividendo(divisoriter_4_dividendoout), .divisor(divisoriter_4_divisorout),
    .cociente(divisoriter_4_cocienteout), .residuo(divisoriter_4_residuoout),
    .dividendoOut(divisoriter_6_dividendoout), .divisorOut(divisoriter_6_divisorout),
    .cocienteOut(divisoriter_6_cocienteout), .residuoOut(divisoriter_6_residuoout));
  divisorIter divisoriter_7 (
    .dividendo(divisoriter_5_dividendoout), .divisor(divisoriter_5_divisorout),
    .cociente(divisoriter_5_cocienteout), .residuo(divisoriter_5_residuoout),
    .dividendoOut(divisoriter_7_dividendoout), .divisorOut(divisoriter_7_divisorout),
    .cocienteOut(divisoriter_7_cocienteout), .residuoOut(divisoriter_7_residuoout));
  divisorIter divisoriter_8 (
    .dividendo(divisoriter_6_dividendoout), .divisor(divisoriter_6_divisorout),
    .cociente(divisoriter_6_cocienteout), .residuo(divisoriter_6_residuoout),
    .dividendoOut(divisoriter_8_dividendoout), .divisorOut(divisoriter_8_divisorout),
    .cocienteOut(divisoriter_8_cocienteout), .residuoOut(divisoriter_8_residuoout));
  divisorIter divisoriter_9 (
    .dividendo(divisoriter_7_dividendoout), .divisor(divisoriter_7_divisorout),
    .cociente(divisoriter_7_cocienteout), .residuo(divisoriter_7_residuoout),
    .dividendoOut(divisoriter_9_dividendoout), .divisorOut(divisoriter_9_divisorout),
    .cocienteOut(divisoriter_9_cocienteout), .residuoOut(divisoriter_9_residuoout));
  divisorIter divisoriter_10 (
    .dividendo(divisoriter_8_dividendoout), .divisor(divisoriter_8_divisorout),
    .cociente(divisoriter_8_cocienteout), .residuo(divisoriter_8_residuoout),
    .dividendoOut(divisoriter_10_dividendoout), .divisorOut(divisoriter_10_divisorout),
    .cocienteOut(divisoriter_10_cocienteout), .residuoOut(divisoriter_10_residuoout));
  divisorIter divisoriter_11 (
    .dividendo(divisoriter_9_dividendoout), .divisor(divisoriter_9_divisorout),
    .cociente(divisoriter_9_cocienteout), .residuo(divisoriter_9_residuoout),
    .dividendoOut(divisoriter_11_dividendoout), .divisorOut(divisoriter_11_divisorout),
    .cocienteOut(divisoriter_11_cocienteout), .residuoOut(divisoriter_11_residuoout));
  divisorIter divisoriter_12 (
    .dividendo(divisoriter_10_dividendoout), .divisor(divisoriter_10_divisorout),
    .cociente(divisoriter_10_cocienteout), .residuo(divisoriter_10_residuoout),
    .dividendoOut(divisoriter_12_dividendoout), .divisorOut(divisoriter_12_divisorout),
    .cocienteOut(divisoriter_12_cocienteout), .residuoOut(divisoriter_12_residuoout));
  divisorIter divisoriter_13 (
    .dividendo(divisoriter_11_dividendoout), .divisor(divisoriter_11_divisorout),
    .cociente(divisoriter_11_cocienteout), .residuo(divisoriter_11_residuoout),
    .dividendoOut(divisoriter_13_dividendoout), .divisorOut(divisoriter_13_divisorout),
    .cocienteOut(divisoriter_13_cocienteout), .residuoOut(divisoriter_13_residuoout));
  divisorIter divisoriter_14 (
    .dividendo(divisoriter_12_dividendoout), .divisor(divisoriter_12_divisorout),
    .cociente(divisoriter_12_cocienteout), .residuo(divisoriter_12_residuoout),
    .dividendoOut(divisoriter_14_dividendoout), .divisorOut(divisoriter_14_divisorout),
    .cocienteOut(divisoriter_14_cocienteout), .residuoOut(divisoriter_14_residuoout));
  divisorIter divisoriter_15 (
    .dividendo(divisoriter_13_dividendoout), .divisor(divisoriter_13_divisorout),
    .cociente(divisoriter_13_cocienteout), .residuo(divisoriter_13_residuoout),
    .dividendoOut(divisoriter_15_dividendoout), .divisorOut(divisoriter_15_divisorout),
    .cocienteOut(divisoriter_15_cocienteout), .residuoOut(divisoriter_15_residuoout));
  divisorIter divisoriter_16 (
    .dividendo(divisoriter_14_dividendoout), .divisor(divisoriter_14_divisorout),
    .cociente(divisoriter_14_cocienteout), .residuo(divisoriter_14_residuoout), .cocienteOut(out_3),
    .residuoOut(out_4));  // open: dividendoOut, divisorOut

  // Other names for the same wires on the sheet: cociente[7:0] = out_3; residuo[7:0] = out_4
endmodule
