// Logisim project divisorIteracion.circ as structural Verilog: 1 circuit, main circuit divisorIter
module divisorIter (
  input  [7:0] dividendo,
  input  [3:0] divisor,
  input  [3:0] cociente,
  input  [3:0] residuo,
  output [7:0] dividendoOut,
  output [3:0] divisorOut,
  output [3:0] cocienteOut,
  output [3:0] residuoOut
);

  wire comparator_1_lt;
  wire [3:0] multiplexer_1_out, subtractor_1_out;

  Multiplexer #(.width(4)) multiplexer_1 (
    .in0({residuo[2:0], 1'b0}), .in1({residuo[2:0], 1'b1}), .out(multiplexer_1_out), .sel(dividendo[7]));
  Comparator #(.width(4)) comparator_1 (.a(multiplexer_1_out), .b(divisor), .lt(comparator_1_lt));  // open: gt, eq
  Subtractor #(.width(4)) subtractor_1 (.a(multiplexer_1_out), .b(divisor), .out(subtractor_1_out));  // open: bin, bout
  Multiplexer #(.width(4)) multiplexer_2 (
    .in0({cociente[2:0], 1'b1}), .in1({cociente[2:0], 1'b0}), .out(cocienteOut), .sel(comparator_1_lt));
  Multiplexer #(.width(4)) multiplexer_3 (
    .in0(subtractor_1_out), .in1(multiplexer_1_out), .out(residuoOut), .sel(comparator_1_lt));

  assign dividendoOut = {dividendo[6:0], 1'b0};
  assign divisorOut = divisor;
endmodule
