// Logisim project idiv.circ as structural Verilog: 1 circuit, main circuit IDIV
module IDIV (
  input  [31:0] XFR1R0N,
  output [23:0] XFA2A1
);

  and and_1 (XFA2A1[17], ~XFA2A1[0], ~XFA2A1[1], ~XFA2A1[2], ~XFA2A1[3], ~XFA2A1[4], ~XFA2A1[5], ~XFA2A1[6], ~XFA2A1[18]);  // AND_Gate
  div div_1 (
    .dividendo(XFR1R0N[23:8]), .divisor(XFR1R0N[7:0]), .out_3({XFA2A1[18], XFA2A1[6:0]}), .out_4(XFA2A1[15:8]));

  assign {XFA2A1[23:19], XFA2A1[16], XFA2A1[7]} = {4'b0000, XFR1R0N[27], XFR1R0N[24], XFA2A1[18]};
endmodule
