// Logisim project imul.circ as structural Verilog: 1 circuit, main circuit IMUL
module IMUL (
  input  [31:0] XFR1R0N,
  output [23:0] XFA2A1
);

  and and_1 (XFA2A1[17], ~XFA2A1[0], ~XFA2A1[1], ~XFA2A1[2], ~XFA2A1[3], ~XFA2A1[4], ~XFA2A1[5], ~XFA2A1[6], ~XFA2A1[7], ~XFA2A1[8], ~XFA2A1[9], ~XFA2A1[10], ~XFA2A1[11], ~XFA2A1[12], ~XFA2A1[13], ~XFA2A1[14], ~XFA2A1[18]);  // AND_Gate
  mult16Bit mult16bit_1 (.A(XFR1R0N[15:8]), .B(XFR1R0N[7:0]), .out_3({XFA2A1[18], XFA2A1[14:0]}));

  assign {XFA2A1[23:19], XFA2A1[16:15]} = {4'b0000, XFR1R0N[27], XFR1R0N[24], XFA2A1[18]};
endmodule
