// Logisim project incalt.circ as structural Verilog: 1 circuit, main circuit INC
module INC (
  input  [31:0] XFR1R0N,
  output [23:0] XFA2A1
);

  and and_1 (XFA2A1[17], ~XFA2A1[0], ~XFA2A1[1], ~XFA2A1[2], ~XFA2A1[3], ~XFA2A1[4], ~XFA2A1[5], ~XFA2A1[6], ~XFA2A1[18]);  // AND_Gate
  Adder adder_1 (.a(XFR1R0N[7:0]), .b(8'h1), .out({XFA2A1[18], XFA2A1[6:0]}), .cin(1'b0), .cout(XFA2A1[16]));
  and and_2 (XFA2A1[19], ~XFR1R0N[7], XFA2A1[18]);  // AND_Gate

  assign {XFA2A1[23:20], XFA2A1[15:7]} = {4'b0000, XFR1R0N[23:16], XFA2A1[18]};
endmodule
