// Logisim project mult16.circ as structural Verilog: 1 circuit, main circuit mult16Bit
module mult16Bit (
  input  [7:0] A,
  input  [7:0] B,
  output [15:0] out_3
);

  wire b0, b1, b2, b3, b4, b5, b6, b7, X;
  wire [7:0] absol_1_out_2;
  wire [15:0] adder_1_out, adder_2_out, adder_3_out, adder_4_out, adder_5_out, adder_6_out, adder_7_out,
       adder_8_out, multiplexer_1_out, multiplexer_2_out, multiplexer_3_out, multiplexer_4_out,
       multiplexer_5_out, multiplexer_6_out, multiplexer_7_out, multiplexer_8_out, not_1_out;

  xor xor_1 (X, B[7], A[7]);
  absol absol_1 (.in_1(A), .out_2(absol_1_out_2));
  absol absol_2 (.in_1(B), .out_2({b7, b6, b5, b4, b3, b2, b1, b0}));
  Multiplexer #(.width(16)) multiplexer_1 (
    .in0({16{1'b0}}), .in1({{8{1'b0}}, absol_1_out_2}), .out(multiplexer_1_out), .sel(b0));
  Multiplexer #(.width(16)) multiplexer_2 (
    .in0({16{1'b0}}), .in1({{7{1'b0}}, absol_1_out_2, 1'b0}), .out(multiplexer_2_out), .sel(b1));
  Multiplexer #(.width(16)) multiplexer_3 (
    .in0({16{1'b0}}), .in1({{6{1'b0}}, absol_1_out_2, 2'b00}), .out(multiplexer_3_out), .sel(b2));
  Multiplexer #(.width(16)) multiplexer_4 (
    .in0({16{1'b0}}), .in1({{5{1'b0}}, absol_1_out_2, 3'b000}), .out(multiplexer_4_out), .sel(b3));
  Multiplexer #(.width(16)) multiplexer_5 (
    .in0({16{1'b0}}), .in1({4'b0000, absol_1_out_2, 4'b0000}), .out(multiplexer_5_out), .sel(b4));
  Multiplexer #(.width(16)) multiplexer_6 (
    .in0({16{1'b0}}), .in1({3'b000, absol_1_out_2, {5{1'b0}}}), .out(multiplexer_6_out), .sel(b5));
  Multiplexer #(.width(16)) multiplexer_7 (
    .in0({16{1'b0}}), .in1({2'b00, absol_1_out_2, {6{1'b0}}}), .out(multiplexer_7_out), .sel(b6));
  Multiplexer #(.width(16)) multiplexer_8 (
    .in0({16{1'b0}}), .in1({1'b0, absol_1_out_2, {7{1'b0}}}), .out(multiplexer_8_out), .sel(b7));
  Adder #(.width(16)) adder_1 (.a(multiplexer_1_out), .b(multiplexer_2_out), .out(adder_1_out));  // open: cin, cout
  Adder #(.width(16)) adder_2 (.a(adder_1_out), .b(multiplexer_3_out), .out(adder_2_out));  // open: cin, cout
  Adder #(.width(16)) adder_3 (.a(adder_2_out), .b(multiplexer_4_out), .out(adder_3_out));  // open: cin, cout
  Adder #(.width(16)) adder_4 (.a(adder_3_out), .b(multiplexer_5_out), .out(adder_4_out));  // open: cin, cout
  Adder #(.width(16)) adder_5 (.a(adder_4_out), .b(multiplexer_6_out), .out(adder_5_out));  // open: cin, cout
  Adder #(.width(16)) adder_6 (.a(adder_5_out), .b(multiplexer_7_out), .out(adder_6_out));  // open: cin, cout
  Adder #(.width(16)) adder_7 (.a(adder_6_out), .b(multiplexer_8_out), .out(adder_7_out));  // open: cin, cout
  assign not_1_out = ~adder_7_out;  // NOT_Gate not_1, 16 bits wide
  Multiplexer #(.width(16)) multiplexer_9 (.in0(adder_7_out), .in1(adder_8_out), .out(out_3), .sel(X));
  Adder #(.width(16)) adder_8 (.a(not_1_out), .b(16'h1), .out(adder_8_out));  // open: cin, cout
endmodule
