// Logisim project mult4Bits.circ as structural Verilog: 1 circuit, main circuit multi4Bits
module multi4Bits (
  input  [3:0] A,
  input  [3:0] B,
  output [7:0] resultado
);

  wire b0, b1, b2, b3, b4;
  wire [3:0] valorabsoluto_2_p1;
  wire [7:0] adder_1_out, adder_2_out, adder_3_out, adder_4_out, multiplexer_1_out, multiplexer_2_out,
       multiplexer_3_out, multiplexer_4_out, not_1_out;

  xor xor_1 (b4, B[3], A[3]);
  // valorAbsoluto valorabsoluto_1: pin names not known; wires that end beside it: B, {b3, b2, b1, b0}
  // valorAbsoluto valorabsoluto_2: pin names not known; wires that end beside it: valorabsoluto_2_p1
  Multiplexer #(.width(8)) multiplexer_1 (
    .in0({8{1'b0}}), .in1({1'b0, valorabsoluto_2_p1, 3'b000}), .out(multiplexer_1_out), .sel(b3));
  Multiplexer #(.width(8)) multiplexer_2 (
    .in0({8{1'b0}}), .in1({4'b0000, valorabsoluto_2_p1}), .out(multiplexer_2_out), .sel(b0));
  Multiplexer #(.width(8)) multiplexer_3 (
    .in0({8{1'b0}}), .in1({3'b000, valorabsoluto_2_p1, 1'b0}), .out(multiplexer_3_out), .sel(b1));
  Multiplexer #(.width(8)) multiplexer_4 (
    .in0({8{1'b0}}), .in1({2'b00, valorabsoluto_2_p1, 2'b00}), .out(multiplexer_4_out), .sel(b2));
  Adder adder_1 (.a(multiplexer_2_out), .b(multiplexer_3_out), .out(adder_1_out), .cin(1'b0));  // open: cout
  Adder adder_2 (.a(adder_1_out), .b(multiplexer_4_out), .out(adder_2_out), .cin(1'b0));  // open: cout
  Adder adder_3 (.a(adder_2_out), .b(multiplexer_1_out), .out(adder_3_out), .cin(1'b0));  // open: cout
  not not_1 (not_1_out[0], adder_3_out[0]);
  not not_2 (not_1_out[1], adder_3_out[1]);
  not not_3 (not_1_out[2], adder_3_out[2]);
  not not_4 (not_1_out[3], adder_3_out[3]);
  not not_5 (not_1_out[4], adder_3_out[4]);
  not not_6 (not_1_out[5], adder_3_out[5]);
  not not_7 (not_1_out[6], adder_3_out[6]);
  not not_8 (not_1_out[7], adder_3_out[7]);
  Adder adder_4 (.a(not_1_out), .b(8'h1), .out(adder_4_out));  // open: cin, cout
  Multiplexer #(.width(8)) multiplexer_5 (.in0(adder_3_out), .in1(adder_4_out), .out(resultado), .sel(b4));

  // Other names for the same wires on the sheet: b5 = B[3]
endmodule
