// Logisim project prueba.circ as structural Verilog: 1 circuit, main circuit juanfernandez
module juanfernandez (
  input  [7:0] in_1,
  output [7:0] out_2,
  output out_3
);

  sum8 sum8_1 (.n1(in_1), .n2(8'h1), .c(1'b0), .res(out_2), .cout(out_3));
endmodule
