// Logisim project resta1Bit.circ as structural Verilog: 1 circuit, main circuit restaBit
module restaBit (
  input  n1,
  input  n2,
  input  cin,
  output res,
  output cout
);

  wire and_1_out, and_2_out, and_3_out, and_4_out, and_5_out, and_6_out, and_7_out, not_1_out, not_2_out,
       not_3_out;

  not not_1 (not_1_out, n1);
  not not_2 (not_2_out, n2);
  not not_3 (not_3_out, cin);
  and and_1 (and_1_out, not_1_out, not_2_out, cin);
  and and_2 (and_2_out, not_1_out, n2, not_3_out);
  and and_3 (and_3_out, n1, not_2_out, not_3_out);
  and and_4 (and_4_out, n1, n2, cin);
  and and_5 (and_5_out, not_2_out, cin);
  and and_6 (and_6_out, n1, not_2_out);
  and and_7 (and_7_out, n1, cin);
  or or_1 (res, and_1_out, and_2_out, and_3_out, and_4_out);
  or or_2 (cout, and_5_out, and_6_out, and_7_out);
endmodule
