// Logisim project resta8Bits.circ as structural Verilog: 1 circuit, main circuit resta8
module resta8 (
  input  [7:0] A,
  input  [7:0] B,
  input  CIN,
  output [7:0] out_4,
  output COUT
);

  wire restabit_1_cout, restabit_2_cout, restabit_3_cout, restabit_4_cout, restabit_5_cout, restabit_6_cout,
       restabit_7_cout;

  restaBit restabit_1 (.n1(B[0]), .n2(A[0]), .cin(CIN), .res(out_4[0]), .cout(restabit_1_cout));
  restaBit restabit_2 (.n1(B[1]), .n2(A[1]), .cin(restabit_1_cout), .res(out_4[1]), .cout(restabit_2_cout));
  restaBit restabit_3 (.n1(B[2]), .n2(A[2]), .cin(restabit_2_cout), .res(out_4[2]), .cout(restabit_3_cout));
  restaBit restabit_4 (.n1(B[3]), .n2(A[3]), .cin(restabit_3_cout), .res(out_4[3]), .cout(restabit_4_cout));
  restaBit restabit_5 (.n1(B[4]), .n2(A[4]), .cin(restabit_4_cout), .res(out_4[4]), .cout(restabit_5_cout));
  restaBit restabit_6 (.n1(B[5]), .n2(A[5]), .cin(restabit_5_cout), .res(out_4[5]), .cout(restabit_6_cout));
  restaBit restabit_7 (.n1(B[6]), .n2(A[6]), .cin(restabit_6_cout), .res(out_4[6]), .cout(restabit_7_cout));
  restaBit restabit_8 (.n1(B[7]), .n2(A[7]), .cin(restabit_7_cout), .res(out_4[7]), .cout(COUT));
endmodule
