// Logisim project rol.circ as structural Verilog: 1 circuit, main circuit ROLalu
module ROLalu (
  input  [31:0] XFR1R0N,
  output [23:0] XFA2A1
);

  and and_1 (XFA2A1[17], ~XFR1R0N[7], ~XFR1R0N[0], ~XFR1R0N[1], ~XFR1R0N[2], ~XFR1R0N[3], ~XFR1R0N[4], ~XFR1R0N[5], ~XFR1R0N[6]);  // AND_Gate

  assign {XFA2A1[23:18], XFA2A1[16:0]} = {4'b0000, XFR1R0N[27], XFR1R0N[6], XFR1R0N[7], XFR1R0N[23:16], XFR1R0N[6:0], XFR1R0N[7]};
endmodule
