// Logisim project sbb.circ as structural Verilog: 1 circuit, main circuit SBB
module SBB (
  input  [31:0] XFR1R0N,
  output [23:0] XFA2A1
);

  wire and_1_out, and_2_out;

  and and_1 (and_1_out, XFR1R0N[15], ~XFR1R0N[7], ~XFA2A1[18]);  // AND_Gate
  and and_2 (and_2_out, ~XFR1R0N[15], XFR1R0N[7], XFA2A1[18]);  // AND_Gate
  and and_3 (XFA2A1[17], ~XFA2A1[0], ~XFA2A1[1], ~XFA2A1[2], ~XFA2A1[3], ~XFA2A1[4], ~XFA2A1[5], ~XFA2A1[6], ~XFA2A1[18]);  // AND_Gate
  resta8 resta8_1 (
    .A(XFR1R0N[15:8]), .B(XFR1R0N[7:0]), .CIN(XFR1R0N[24]), .out_4({XFA2A1[18], XFA2A1[6:0]}),
    .COUT(XFA2A1[16]));
  or or_1 (XFA2A1[19], and_1_out, and_2_out);

  assign {XFA2A1[23:20], XFA2A1[15:7]} = {4'b0000, XFR1R0N[23:16], XFA2A1[18]};

  // Other names for the same wires on the sheet: B = XFR1R0N[7]; A = XFR1R0N[15]
endmodule
