// Logisim project sub.circ as structural Verilog: 1 circuit, main circuit SUBalu
module SUBalu (
  input  [31:0] XFR1R0N,
  output [23:0] XFA2A1
);

  and and_1 (XFA2A1[17], ~XFA2A1[0], ~XFA2A1[1], ~XFA2A1[2], ~XFA2A1[3], ~XFA2A1[4], ~XFA2A1[5], ~XFA2A1[6], ~XFA2A1[18]);  // AND_Gate
  resta8 resta8_1 (
    .A(XFR1R0N[15:8]), .B(XFR1R0N[7:0]), .CIN(1'b0), .out_4({XFA2A1[18], XFA2A1[6:0]}), .COUT(XFA2A1[16]));

  assign {XFA2A1[23:20], XFA2A1[15:7]} = {4'b0000, XFR1R0N[23:16], XFA2A1[18]};

  // Other names for the same wires on the sheet: A = XFR1R0N[7]; B = XFR1R0N[15]
endmodule
