// Logisim project sum8Bit.circ as structural Verilog: 1 circuit, main circuit sum8
module sum8 (
  input  [7:0] n1,
  input  [7:0] n2,
  input  c,
  output [7:0] res,
  output cout
);

  wire sum1bit_1_cout, sum1bit_2_cout, sum1bit_3_cout, sum1bit_4_cout, sum1bit_5_cout, sum1bit_6_cout,
       sum1bit_7_cout;

  sum1Bit sum1bit_1 (.n1(n1[0]), .n2(n2[0]), .cin(c), .res(res[0]), .cout(sum1bit_1_cout));
  sum1Bit sum1bit_2 (.n1(n1[1]), .n2(n2[1]), .cin(sum1bit_1_cout), .res(res[1]), .cout(sum1bit_2_cout));
  sum1Bit sum1bit_3 (.n1(n1[2]), .n2(n2[2]), .cin(sum1bit_2_cout), .res(res[2]), .cout(sum1bit_3_cout));
  sum1Bit sum1bit_4 (.n1(n1[3]), .n2(n2[3]), .cin(sum1bit_3_cout), .res(res[3]), .cout(sum1bit_4_cout));
  sum1Bit sum1bit_5 (.n1(n1[4]), .n2(n2[4]), .cin(sum1bit_4_cout), .res(res[4]), .cout(sum1bit_5_cout));
  sum1Bit sum1bit_6 (.n1(n1[5]), .n2(n2[5]), .cin(sum1bit_5_cout), .res(res[5]), .cout(sum1bit_6_cout));
  sum1Bit sum1bit_7 (.n1(n1[6]), .n2(n2[6]), .cin(sum1bit_6_cout), .res(res[6]), .cout(sum1bit_7_cout));
  sum1Bit sum1bit_8 (.n1(n1[7]), .n2(n2[7]), .cin(sum1bit_7_cout), .res(res[7]), .cout(cout));

  // Other names for the same wires on the sheet: R[7:0] = res
endmodule
