// Logisim project valorAbsoluto.circ as structural Verilog: 1 circuit, main circuit absol
module absol (
  input  [7:0] in_1,
  output [7:0] out_2
);

  wire [7:0] not_1_out, sum8_1_res;

  assign not_1_out = ~in_1;  // NOT_Gate not_1, 8 bits wide
  Multiplexer #(.width(8)) multiplexer_1 (.in0(in_1), .in1(sum8_1_res), .out(out_2), .sel(in_1[7]));
  sum8 sum8_1 (.n1(not_1_out), .n2(8'h1), .c(1'b0), .res(sum8_1_res));  // open: cout
endmodule
