// Logisim project xchg.circ as structural Verilog: 1 circuit, main circuit XCHG
module XCHG (
  input  [31:0] XFR1R0N,
  output [23:0] XFA2A1
);


  assign XFA2A1 = {XFR1R0N[31:24], XFR1R0N[15:8], XFR1R0N[23:16]};
endmodule
